# Fritzing sketch salak-skematik (saved by Fritzing 0.9.3b)
breadboards: 1

parts:
  A2 = JXBS-3001-NPK-RS smaller
  VCC3 = Battery  # not connected
  M6 = MAX485 Breakout [package=THT]
  Display2 = LCD screen 16x2 IIC [part_number=101290]
  S3 = Round Pushbutton  # not connected
  M8 = DOIT Esp32 DevKit v1 (30 pins long, 11 pins width) [part_number=ESP32S-PIN30]
  VCC4 = Battery
  A3 = JXBS-3001-NPK-RS smaller
  M9 = MAX485 Breakout [package=THT]
  M10 = MT3608 Module
  S4 = Round Pushbutton  # not connected
  M11 = DOIT Esp32 DevKit v1 (30 pins long, 11 pins width) [part_number=ESP32S-PIN30]
  LCD2004-I2C1 = LCD2004-I2C
  VCC7 = Battery
  VCC8 = Battery  # not connected
  S5 = SPST Switch [package=r_sw_th]  # not connected

nets:
  N1: A2.Pin_3, M6.B
  N2: A2.Pin_4, M6.A
  N3: M6.RO, M8.D19
  N4: M6.RE, M8.D21
  N5: M6.DE, M8.D22
  N6: M6.DI, M8.D23
  GND: M6.GND, Display2.GND, M8.GND, VCC4.-
  VCC: M6.VCC, M8.VIN, VCC4.+
  VCC_2: Display2.VCC, M8.3V3
  N7: Display2.SDA, M8.D4
  N8: Display2.SCL, M8.D2
  N9: A3.Pin_1, M10.pin3
  N10: A3.Pin_2, M10.pin4
  N11: A3.Pin_3, M9.B
  N12: A3.Pin_4, M9.A
  N13: M10.pin1, VCC7.-
  N14: M10.pin2, VCC7.+
  3V3: M11.3V3, LCD2004-I2C1.VCC
  GND_2: M11.GND, LCD2004-I2C1.GND
  N15: M11.D21, LCD2004-I2C1.SDA
  N16: M11.D22, LCD2004-I2C1.SCL

custom parts:
  JXBS-3001-NPK-RS smaller: The NPK sensor is designed for detecting the content of nitrogen, phosphorus and potassium in soil, determining the fertility of the soil and facilitating the evaluation of the soil condition by the customer system. This version has breadboard reduced in size to more closely match the 485 adapter and CPU board.
  Battery: Your standard 2x 18650 battery pack (7,4 Volts)
  MAX485 Breakout: MAX485 RS485 breakout board
  LCD screen 16x2 IIC: LCD screen with HD44780 controller enables showing text, symbols, value or anything else that comes from Croduino/Arduino. It is capable of showing 16 symbols in two lines and therefore can be used in many projects that need to send clearly visible and legible output information.. • Color of symbols: White • Backlight: Blue • Dimensions: 80 x 36 x 12 mm • Screen dimensions: 64.5 x 16 mm •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
  DOIT Esp32 DevKit v1 (30 pins long, 11 pins width): The DOIT Esp32 DevKit v1 is one of the development board created by DOIT to evaluate the ESP-WROOM-32 module. It is based on the ESP32 microcontroller that boasts Wifi, Bluetooth, Ethernet and Low Power support all in a single chip. (vanepp) made breadboard work, adjusted pin numbering and labels and reduced size of schematic and cleaned up pcb. This chip is 30pins long (2 x15) and 11 pins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
  MT3608 Module: MT3608 Boost Converter Module Links: Aerosemi MT3608 2A Step Up Converter datasheet
  LCD2004-I2C: A standard character display with 4x20 characters. Comes in many colors with LCM2004 IIC attached.
